# Fritzing sketch treat_dispenser (saved by Fritzing 0.9.3b)

parts:
  U1 = ESP32S-HiLetgo [part_number=ESP32S-HiLetgo]
  Pololu_A1 = Pololu A4988 [package=SO16]
  M1 = Stepper Motor - Bipolar
  C1 = Capacitor Polarized [package=cpol-radial-100uf-25v]
  V1 = DC Power [voltage=12V]
  M2 = RioRand LM2596
  Part2 = Mono 2.5W Class D Audio Amplifier - PAM8302
  SP1 = SPEAKER [package=pcb_mount_speaker]

nets:
  N1: U1.3.3, Pololu_A1.RESET, Pololu_A1.SLEEP, Pololu_A1.VDD
  N2: U1.GPIO32, Pololu_A1.DIR
  N3: U1.GPIO33, U1.GPIO9, Pololu_A1.ENABLE
  N4: U1.GPIO25, Part2.AIN+
  N5: U1.GPIO26, Pololu_A1.MS2
  N6: U1.GPIO27, Pololu_A1.MS3
  N7: U1.GPIO14, Pololu_A1.STEP
  GND: U1.GND, Pololu_A1.GND, M2.Pin_2, M2.Pin_4, Part2.GND, Part2.AIN-
  VIN: U1.VIN, M2.Pin_3, Part2.VCC
  N8: U1.GPIO16, Part2.SD
  N9: U1.GPIO17, Pololu_A1.MS1
  N10: Pololu_A1.1B, M1.D
  N11: Pololu_A1.1A, M1.B
  N12: Pololu_A1.2A, M1.C
  N13: Pololu_A1.2B, M1.A
  N14: Pololu_A1.VMOT, C1.+
  N15: C1.-, V1.V+, M2.Pin_1
  N16: Part2.VO+, SP1.-
  N17: Part2.VO-, SP1.+

custom parts:
  ESP32S-HiLetgo: HiLetgo ESP-WROOM-32 ESP32 ESP-32S Development Board 2.4GHz Dual-Mode WiFi + Bluetooth Dual Cores Microcontroller The ESP32 integrated with Antenna switches, RF Balun, power amplifiers, low-noise amplifiers, filters, and management modules, and the entire solution occupies the least area of PCB. 2.4 GHz Wi-Fi plus Bluetooth dual-mode chip, with TSMC Ultra-low power consumption 40nm technology,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
  Mono 2.5W Class D Audio Amplifier - PAM8302: A super small but powerful mono amplifier able to deliver up to 2.5 Watts into 4-8 ohm impedance speakers. Inside the miniature chip is a class D controller, able to run from 2.0V-5.5VDC. Since the amp is a class D, its very efficient (over 90% efficient when driving an 8Ω speaker at over half a Watt) - making it perfect for portable and battery-powered projects.
